# Fritzing sketch Temp&Photoresistor Sketch (saved by Fritzing 0.9.3b)
breadboards: 1

parts:
  U1 = NodeMCU V3.0
  VCC1 = 4 x AAA Battery Mount
  IC1 = L293D [package=THT]
  DHT1 = DHT11 Humitidy and Temperature Sensor
  LED1 = smd LED [color="Red (633nm)" package="0805 [SMD]"]
  LED2 = smd LED [color="Red (633nm)" package="0603 [SMD]"]
  R2 = PHOTOCELL [package=photocell]
  M1 = DC Motor
  R3 = Resistor [tolerance=±5% resistance=220 package=THT]
  R4 = Resistor [tolerance=±5% resistance=220 package=THT]
  R5 = Resistor [tolerance=±5% resistance=220 package=THT]

nets:
  N1: U1.D0, DHT1.DATA
  N2: U1.D1, IC1.In_2
  N3: U1.D2, IC1.In_1
  N4: U1.D3, IC1.Enable_1
  3V3: U1.3V3, VCC1.-, VCC1.+, IC1.0V, IC1.+Vmotor, IC1.+V, DHT1.VDD, R2.P$2, R3.Pin_1, R4.Pin_1, R5.Pin_1
  N5: U1.GND#6, U1.GND#13, U1.GND#16, U1.GND#33
  N6: U1.D7, LED2.cathode
  N7: U1.D8, LED1.cathode
  N8: U1.A0, R2.P$1
  N9: IC1.Out_1_(_Controlled_by_Enable_1_), M1.pin_2
  N10: IC1.Out_2_(_Controlled_by_Enable_1_), M1.pin_1
  N11: DHT1.GND, R5.Pin_0
  N12: LED1.anode, R4.Pin_0
  N13: LED2.anode, R3.Pin_0

custom parts:
  NodeMCU V3.0: ESP8266 based NodeMCU
  DHT11 Humitidy and Temperature Sensor: DHT11 Humidity and Temperature Sensor
